# Fritzing sketch Receiver (saved by Fritzing 0.9.3b)
circuit board: 12.4cm x 8.8cm
breadboards: 1

parts:
  Teensy_3_1 = Teensy 3.1
  J1 = shrouded pin header, 16 pins [form="♂ (shrouded male)"]
  Part2 = NRF24L01+ Breakout Board
  U2 = LIPO-2000mAh [package=lipo-2000]
  S2 = SPST Switch [package=ayz0202]
  Part3 = Adafruit Bluefruit LE UART Friend [part_number="Adafruit #2479"]
  Reg1 = DC-DC CONVERTER [part_number=80633 package=dc-dc_converter]
  JP2 = Header 4 [package=screwterminal-3.5mm-4_lock]
  C1 = Capacitor Polarized [package=cpol-radial-10uf-25v]

nets:
  GND: Teensy_3_1.GND, J1.pin9, J1.pin13, J1.pin15, Part2.GND, U2.-, Part3.GND, Part3.CTS, Reg1.IN-, C1.-
  N1: Teensy_3_1.D0, Part2.CE
  N2: Teensy_3_1.D1, Part2.CS
  N3: Teensy_3_1.D2, J1.pin1
  N4: Teensy_3_1.D3, Teensy_3_1.D8, J1.pin10
  N5: Teensy_3_1.D4, J1.pin8
  N6: Teensy_3_1.D5, J1.pin16
  N7: Teensy_3_1.D6, J1.pin2
  N8: Teensy_3_1.D7, J1.pin14
  N9: Teensy_3_1.D9, J1.pin5
  N10: Teensy_3_1.D10, J1.pin12
  N11: Teensy_3_1.D11, Part2.MOSI
  N12: Teensy_3_1.D12, Part2.MISO
  3V3: Teensy_3_1.3V3, Part2.VCC, Part3.VIN, C1.+
  N13: Teensy_3_1.D13, Part2.SCK
  N14: Teensy_3_1.A0/D14, J1.pin7
  N15: Teensy_3_1.A2/D16, Part3.TXO
  N16: Teensy_3_1.A3/D17, Part3.RXI
  N17: Teensy_3_1.A6/D20, J1.pin4
  N18: Teensy_3_1.A7/D21, J1.pin3
  N19: Teensy_3_1.A8/D22, J1.pin6
  N20: Teensy_3_1.A9/D23, J1.pin11
  N21: Teensy_3_1.Vin, S2.P, S2.S, Reg1.IN+
  N22: U2.+, S2.O
  N23: Reg1.OUT-, JP2.3, JP2.4
  N24: Reg1.OUT+, JP2.1, JP2.2

custom parts:
  Adafruit Bluefruit LE UART Friend: The Bluefruit LE UART Friend makes it easy to add Bluetooth Low Energy connectivity to anything with a hardware or software serial port. We even have nice hardware flow control so you won't have to think about losing data. Connect to your Arduino or other microcontroller or even just a standard FTDI cable for debugging and testing.
  DC-DC CONVERTER: WYHP 5A constant current/voltage manufactured by Shenzhen Weiyapuhua Technology Co., Ltd
